# Fritzing sketch atari-600xl-pbi-nolevel (saved by Fritzing 0.9.9b)
circuit board: 10.811cm x 6.84322cm
breadboards: 1

parts:
  LEVELSHT-1 = Adafruit 4-channel I2C-safe Bi-directional Logic Level Converter [part_number="Adafruit #757"]
  U1 = ESP32-38PinWide [part_number=ESP32-38Pin]
  R1 = Resistor [tolerance=±5% resistance=10k power=0.25 package=THT]
  J1 = shrouded pin header, 50 pins [form="♂ (shrouded male)"]
  R2 = Resistor [tolerance=±5% resistance=10k power=0.25 package=THT]
  R3 = Resistor [tolerance=±5% resistance=220 power=0.25 package=THT]
  SPI-TFT = female pin header, 8 pins [form="♀ (female)"]
  LEVELSHT-2 = Adafruit 4-channel I2C-safe Bi-directional Logic Level Converter [part_number="Adafruit #757"]
  MIC = Breakout Board for Electret Microphone
  LEVELSHT-3 = Adafruit 4-channel I2C-safe Bi-directional Logic Level Converter [part_number="Adafruit #757"]

nets:
  GND: LEVELSHT-1.GND, U1.GND, J1.pin1, J1.pin10, J1.pin15, J1.pin26, J1.pin30, J1.pin35, J1.pin36, R2.Pin_1, SPI-TFT.pin2, LEVELSHT-2.GND, MIC.GND, LEVELSHT-3.GND
  CS/ESP_MPD: LEVELSHT-1.A4, U1.GPIO15, SPI-TFT.pin3
  DCRS/ESP_ES: LEVELSHT-1.A3, U1.GPIO8, SPI-TFT.pin5
  ESP_RDY/MOSI: LEVELSHT-1.A2, U1.GPIO7, SPI-TFT.pin6
  ESP_IRQ/SCLK: LEVELSHT-1.A1, U1.GPIO6, SPI-TFT.pin7
  3.3V: LEVELSHT-1.LV, U1.3.3, SPI-TFT.pin1, SPI-TFT.pin8, LEVELSHT-2.LV, MIC.VCC, LEVELSHT-3.LV
  MPD_I: LEVELSHT-1.B4, J1.pin22
  ES_I: LEVELSHT-1.B3, J1.pin50
  RDY_I: LEVELSHT-1.B2, J1.pin33
  IRQ_I: LEVELSHT-1.B1, J1.pin18
  5V: LEVELSHT-1.HV, U1.VIN, J1.pin24, J1.pin27, LEVELSHT-2.HV, LEVELSHT-3.HV
  RST33: U1.EN, R1.Pin_1, R2.Pin_0, SPI-TFT.pin4
  PH2_O: U1.GPIO36, J1.pin16
  RW_O: U1.GPIO39, J1.pin28
  REF_O: U1.GPIO34, J1.pin31
  ESP_D7: U1.GPIO35, LEVELSHT-2.A4
  ESP_D5: U1.GPIO32, LEVELSHT-2.A3
  ESP_D3: U1.GPIO33, LEVELSHT-2.A2
  ESP_D1: U1.GPIO25, LEVELSHT-2.A1
  A15_O: U1.GPIO26, J1.pin41
  A14_O: U1.GPIO27, J1.pin42
  A12_O: U1.GPIO14, J1.pin43
  A10_O: U1.GPIO12, J1.pin44
  A8_O: U1.GPIO13, J1.pin45
  A5_O: U1.GPIO9, J1.pin47
  A3_O: U1.GPIO10, J1.pin48
  A1_O: U1.GPIO11, J1.pin49
  ESP_MIC: U1.GPIO2, R3.Pin_1
  A0_O: U1.GPIO0, J1.pin2
  A2_0: U1.GPIO4, J1.pin3
  A4_O: U1.GPIO16, J1.pin4
  A6_O: U1.GPIO17, J1.pin5
  A7_O: U1.GPIO5, J1.pin6
  A9_O: U1.GPIO18, J1.pin7
  A11_O: U1.GPIO19, J1.pin8
  A13_O: U1.GPIO21, J1.pin9
  ESP_D6: U1.GPIO3, LEVELSHT-3.A1
  ESP_D4: U1.GPIO1, LEVELSHT-3.A2
  ESP_D2: U1.GPIO22, LEVELSHT-3.A3
  ESP_D0: U1.GPIO23, LEVELSHT-3.A4
  RST_O: R1.Pin_0, J1.pin34
  D0_IO: J1.pin11, LEVELSHT-3.B4
  D2_IO: J1.pin12, LEVELSHT-3.B3
  D4_IO: J1.pin13, LEVELSHT-3.B2
  D6_IO: J1.pin14, LEVELSHT-3.B1
  NOT CONNECTED 1: J1.pin17
  NOT CONNECTED 2: J1.pin19
  NOT CONNECTED 3: J1.pin20
  CAS_O: J1.pin21
  UNUSED GND 1: J1.pin23
  AUD_I: J1.pin25
  RAS_O: J1.pin29
  CASINH_O: J1.pin32
  D7_IO: J1.pin37, LEVELSHT-2.B4
  D5_IO: J1.pin38, LEVELSHT-2.B3
  D3_IO: J1.pin39, LEVELSHT-2.B2
  D1_IO: J1.pin40, LEVELSHT-2.B1
  UNUSED GND 2: J1.pin46
  N1: R3.Pin_0, MIC.AUD

notes:
  1) https://www.amazon.com/Connector-40p-98-Finger-Through-Durable/dp/B09MZXJ8Q3/ref=sr_1_15?crid=XJIJ1S8Y0NPS&keywords=edge%2Bconnector%2B0.1%2Binches&qid=1644340803&sprefix=edge%2Bconnector%2B0.1%2Binches%2Caps%2C406&sr=8-15&th=1
  2) https://www.amazon.com/HiLetgo-ESP-WROOM-32-Development-Microcontroller-Integrated/dp/B0718T232Z/ref=sr_1_10?keywords=ESP32+38+pin&qid=1644360022&sr=8-10
  3) https://www.amazon.com/KeeYees-Channels-Converter-Bi-Directional-Shifter/dp/B07LG646VS/ref=sr_1_3?keywords=4-channel+I2C-safe+Bi-directional+Logic+Level+Converter+-+BSS138&qid=1644509232&sr=8-3
  unused pins

custom parts:
  Adafruit 4-channel I2C-safe Bi-directional Logic Level Converter: Because the Arduino (and Basic Stamp) are 5V devices, and most modern sensors, displays, flash cards and modes are 3.3V-only, many makers find that they need to perform level shifting/conversion to protect the 3.3V device from 5V. We do have some other handy level shifters in the shop, from the DIP 74LVC245 to the fancy bi-directional TXB0108. However, neither of these are happy to work with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
  ESP32-38PinWide: Generic 38-Pin ESP32 with wide format (only access to one side of pins on a breadboard) based on Stephen Lilley's HiLetgo ESP-WROOM-32 ESP32 ESP-32S Development Board.
